// Logisim project Project2Given.circ as structural Verilog: 4 circuits, main circuit main
module main (
);

  wire and_1_out, and_2_out, B0, B1, B2, B3, B4, B5, B6, B7, B8, B9, BL, BU, C0, C1, C2, CLK, L1_l, L1_u,
       not_1_out, or_8_out, P1_v, R0, R1, R3, R4, Valid;
  wire [2:0] counter_1_q;
  wire [3:0] IB1_c0, P1_b0, register_2_q, register_3_q, register_4_q, register_5_q;

  Button n1 (.out(B1));
  Button n4 (.out(B4));
  Button n7 (.out(B7));
  Button L (.out(BL));
  Button n3 (.out(B3));
  Button n2 (.out(B2));
  Button n6 (.out(B6));
  Button n5 (.out(B5));
  Button n9 (.out(B9));
  Button n8 (.out(B8));
  Button U (.out(BU));
  Button n0 (.out(B0));
  or or_1 (R0, B3, B2, B1);
  or or_2 (R1, B6, B5, B4);
  or or_3 (R3, B9, B8, B7);
  or or_4 (R4, BU, B0, BL);
  or or_5 (C0, B1, B4, B7, BL);
  or or_6 (C1, B2, B5, B8, B0);
  or or_7 (C2, B3, B6, B9, BU);
  Clock clock_1 (.out(CLK));
  nand nand_1 (Valid, IB1_c0[0], IB1_c0[1], IB1_c0[2], IB1_c0[3]);
  // Probe on P1_b0
  Panel P1 (
    .R0(R0), .R1(R1), .R2(R3), .R3(R4), .C0(C0), .C1(C1), .C2(C2), .B0(P1_b0[0]), .B1(P1_b0[1]),
    .B2(P1_b0[2]), .B3(P1_b0[3]), .V(P1_v));
  LED Press (.in(P1_v));
  // Probe on IB1_c0
  InputBuffer IB1 (
    .B0(P1_b0[0]), .B1(P1_b0[1]), .B2(P1_b0[2]), .B3(P1_b0[3]), .V(P1_v), .CLK(not_1_out), .C0(IB1_c0[0]),
    .C1(IB1_c0[1]), .C2(IB1_c0[2]), .C3(IB1_c0[3]));
  not not_1 (not_1_out, CLK);
  Register #(.width(4)) register_1 (.D(register_2_q), .en(Valid), .clk(CLK));  // open: Q, clr
  Lock L1 (.C0(IB1_c0[0]), .C1(IB1_c0[1]), .C2(IB1_c0[2]), .C3(IB1_c0[3]), .CLK(CLK), .L(L1_l), .U(L1_u));
  Counter #(.max('h7), .width(3)) counter_1 (
    .count(or_8_out), .Q(counter_1_q), .up(L1_u), .clk(CLK));  // open: load, D, carry, clr
  or or_8 (or_8_out, L1_l, L1_u);
  Register #(.width(4)) register_2 (.D(register_3_q), .en(Valid), .clk(CLK), .Q(register_2_q));  // open: clr
  LED Unlocked (.in(and_1_out));
  and and_1 (and_1_out, ~counter_1_q[0], ~counter_1_q[1], ~counter_1_q[2]);  // AND_Gate
  Register #(.width(4)) register_3 (.D(register_4_q), .en(Valid), .clk(CLK), .Q(register_3_q));  // open: clr
  LED Locked (.in(and_2_out));
  and and_2 (and_2_out, ~counter_1_q[0], ~counter_1_q[1], counter_1_q[2]);  // AND_Gate
  Register #(.width(4)) register_4 (.D(register_5_q), .en(Valid), .clk(CLK), .Q(register_4_q));  // open: clr
  Register #(.width(4)) register_5 (.D(IB1_c0), .en(Valid), .clk(CLK), .Q(register_5_q));  // open: clr
endmodule

module Panel (
  input  R0,
  input  R1,
  input  R2,
  input  R3,
  input  C0,
  input  C1,
  input  C2,
  output B0,
  output B1,
  output B2,
  output B3,
  output V
);

  wire L, U, x1, x2, x3, x4, x5, x6, x7, x8, x9, xor_1_out, xor_2_out;

  and and_1 (x1, R0, C0);
  and and_2 (x2, R0, C1);
  and and_3 (x3, R0, C2);
  and and_4 (x4, R1, C0);
  and and_5 (x5, R1, C1);
  and and_6 (x6, R1, C2);
  and and_7 (x7, R2, C0);
  and and_8 (x8, R2, C1);
  and and_9 (x9, R2, C2);
  and and_10 (L, R3, C0);
  and and_11 (U, R3, C2);
  or or_1 (B0, x1, x3, x5, x7, x9);
  or or_2 (B1, x2, x3, x6, x7, L, U);
  or or_3 (B2, x4, x5, x6, x7, U);
  or or_4 (B3, x8, x9, L, U);
  ExactlyOne xor_1 (.out(xor_1_out), .in0(R0), .in1(R1), .in2(R2), .in3(R3));
  ExactlyOne xor_2 (.out(xor_2_out), .in0(C0), .in1(C1), .in2(C2));
  and and_12 (V, xor_1_out, xor_2_out);
endmodule

module InputBuffer (
  input  B0,
  input  B1,
  input  B2,
  input  B3,
  input  V,
  input  CLK,
  output C0,
  output C1,
  output C2,
  output C3
);

  wire and_1_out, and_2_out, and_3_out, and_4_out, not_1_out, not_2_out, not_3_out, not_4_out, not_5_out,
       not_6_out, not_7_out, not_8_out;

  not not_1 (not_1_out, B0);
  not not_2 (not_2_out, B1);
  not not_3 (not_3_out, B2);
  not not_4 (not_4_out, B3);
  and and_1 (and_1_out, not_1_out, V);
  and and_2 (and_2_out, not_2_out, V);
  and and_3 (and_3_out, not_3_out, V);
  and and_4 (and_4_out, not_4_out, V);
  not not_5 (not_5_out, and_1_out);
  not not_6 (not_6_out, and_2_out);
  not not_7 (not_7_out, and_3_out);
  not not_8 (not_8_out, and_4_out);
  D_Flip_Flop d_ff_1 (.D(not_5_out), .clk(CLK), .Q(C0));  // open: Qn, preset, reset
  D_Flip_Flop d_ff_2 (.D(not_6_out), .clk(CLK), .Q(C1));  // open: Qn, preset, reset
  D_Flip_Flop d_ff_3 (.D(not_7_out), .clk(CLK), .Q(C2));  // open: Qn, preset, reset
  D_Flip_Flop d_ff_4 (.D(not_8_out), .clk(CLK), .Q(C3));  // open: Qn, preset, reset
endmodule

module Lock (
  input  C0,
  input  C1,
  input  C2,
  input  C3,
  input  CLK,
  output L,
  output U
);

  wire L1, not_1_out, not_2_out, not_3_out, not_4_out, not_5_out, not_6_out, not_7_out, not_8_out,
       register_1_q, register_2_q, register_3_q, register_4_q, register_5_q, register_6_q, register_7_q,
       register_8_q;

  and and_1 (U, C0, C1, C2, C3);
  not not_1 (not_1_out, C0);
  not not_2 (not_2_out, C2);
  not not_3 (not_3_out, C0);
  not not_4 (not_4_out, C2);
  and and_2 (L, not_1_out, C1, not_2_out, C3);
  // AND_Gate and_3 has open pins: in0=not_3_out, in1=C1, in2=not_4_out, in3=C3, out=open
  Register #(.width(1)) register_1 (.D(C0), .en(L), .clk(CLK), .Q(register_1_q));  // open: clr
  Register #(.width(1)) register_2 (.D(C1), .en(L), .clk(CLK), .Q(register_2_q));  // open: clr
  Register #(.width(1)) register_3 (.D(C2), .en(L), .clk(CLK), .Q(register_3_q));  // open: clr
  Register #(.width(1)) register_4 (.D(C3), .en(L), .clk(CLK), .Q(register_4_q));  // open: clr
  Register #(.width(1)) register_5 (.D(C0), .clk(CLK), .Q(register_5_q));  // open: en, clr
  Register #(.width(1)) register_6 (.D(C1), .clk(CLK), .Q(register_6_q));  // open: en, clr
  Register #(.width(1)) register_7 (.D(C2), .clk(CLK), .Q(register_7_q));  // open: en, clr
  Register #(.width(1)) register_8 (.D(C3), .clk(CLK), .Q(register_8_q));  // open: en, clr
  not not_5 (not_5_out, register_1_q);
  not not_6 (not_6_out, register_3_q);
  not not_7 (not_7_out, register_5_q);
  not not_8 (not_8_out, register_7_q);
  and and_4 (L1, not_5_out, register_2_q, not_6_out, register_4_q);
  // AND_Gate and_5 has open pins: in0=L1, in1=not_7_out, in2=register_6_q, in3=not_8_out, in4=register_8_q, out=open
endmodule
